# Fritzing sketch Method B (saved by Fritzing 0.9.3b)
circuit board: 8.46667cm x 5.64444cm
breadboards: 1

parts:
  R1 = Rotary Potentiometer (Large) [maximum_resistance=100kΩ package=THT]
  U1 = LCD-16X2 [package=lcd-16x2]
  Part1 = Arduino Mega 2560 (Rev3)
  LED1 = smd LED [color="Red (633nm)" package="1206 [SMD]"]
  Keypad4x1 = Keypad Membran 4x4
  hc-sr1 = hc-sr04
  J1 = Buzzer
  hc-sr3 = hc-sr04

nets (from the breadboard view):
  GND: R1.leg1, U1.VSS, U1.R_W, U1.K, Part1.GND, LED1.cathode, hc-sr1.GND, hc-sr3.GND
  N1: R1.wiper, U1.VO
  VCC: R1.leg2, U1.A, Part1.5V, hc-sr1.VCC, J1.pin1, hc-sr3.VCC
  N2: U1.RS, Part1.D7_PWM
  N3: U1.E, Part1.D8_PWM
  N4: U1.DB4, Part1.D9_PWM
  N5: U1.DB5, Part1.D10_PWM
  N6: U1.DB6, Part1.D11_PWM
  N7: U1.DB7, Part1.D12_PWM
  N8: Part1.D13_PWM, LED1.anode, J1.pin2
  N9: Part1.D2_PWM, hc-sr3.Echo
  N10: Part1.D3_PWM, hc-sr3.Trig
  N11: Part1.D22, hc-sr1.Echo
  N12: Part1.D24, hc-sr1.Trig
  N13: Part1.D31, Keypad4x1.Pin1
  N14: Part1.D32, Keypad4x1.Pin2
  N15: Part1.D33, Keypad4x1.Pin3
  N16: Part1.D39, Keypad4x1.Pin4
  N17: Part1.D41, Keypad4x1.Pin5
  N18: Part1.D43, Keypad4x1.Pin6
  N19: Part1.D45, Keypad4x1.Pin7
  N20: Part1.D49, Keypad4x1.Pin8

custom parts:
  Keypad Membran 4x4: Membrane Keypad 4x4 Matrix
  Buzzer: Fixed frequency buzzer

// code stored in the sketch: Code B.ino
#include <HCSR04.h>
#include <Keypad.h>
#define echoPin 22// mask picking
#define trigPin 24
#define echoPin2 3//motion sensing
#define trigPin2 2

// include the library code:
#include <LiquidCrystal.h>
//********************************************************************
// initialize the library with the numbers of the interface pins
LiquidCrystal lcd(7, 8, 9, 10, 11, 12);

int red=13 ;// led triggered by the motion
int green = 5;//mask picked
int buzzer= 13;
int distance;
int motion;
int duration;
int duration2;
//lcd initializations
const byte ROWS = 4; //four rows
const byte COLS = 4; //four columns
//define the cymbols on the buttons of the keypads
char keys[ROWS][COLS] = {
  {'1','2','3','A'},
  {'4','5','6','B'},
  {'7','8','9','C'},
  {'*','0','#','D'}
};
byte rowPins[ROWS] = {31, 32, 33, 39}; //connect to the row pinouts of the keypad
byte colPins[COLS] = {41, 43, 45, 49}; //connect to the column pinouts of the keypad
Keypad kpd = Keypad( makeKeymap(keys), rowPins, colPins, ROWS, COLS ); 

// int facemasks
int facemask = 0;
 
 void setup() 
   {
          Serial.begin(9600);
  
           pinMode(trigPin,OUTPUT);
            pinMode (echoPin, INPUT);
             pinMode(trigPin2,OUTPUT);
              pinMode (echoPin2, INPUT);
  // set up the LCD's number of columns and rows:
       lcd.begin(16, 2);
       pinMode(buzzer, OUTPUT); 
        pinMode(red, OUTPUT);
         pinMode(green, OUTPUT);
         
   }

void loop()
{
//*************************************************
//case 1: when there is no face mask (intialization)
 digitalWrite(red,LOW);
 digitalWrite(green, LOW);
  int fm_temp = 0;
  while(facemask==0)
     {
       lcd.setCursor(0,0);
         lcd.print("Number of mask:");
           lcd.setCursor(0,1);
             lcd.print("Max 100: ");

//input number of face mask

             char key = kpd.getKey();
            if(key){
            if(key == '0') fm_temp = fm_temp * 10 + 0;
            if(key == '1') fm_temp = fm_temp * 10 + 1;
            if(key == '2') fm_temp = fm_temp * 10 + 2;
            if(key == '3') fm_temp = fm_temp * 10 + 3;
            if(key == '4') fm_temp = fm_temp * 10 + 4;
            if(key == '5') fm_temp = fm_temp * 10 + 5;
            if(key == '6') fm_temp = fm_temp * 10 + 6;
            if(key == '7') fm_temp = fm_temp * 10 + 7;
            if(key == '8') fm_temp = fm_temp * 10 + 8;
            if(key == '9') fm_temp = fm_temp * 10 + 9;
            if(key == 'C') fm_temp = fm_temp / 10;

         lcd.setCursor(9,1);
           lcd.print(fm_temp);
             lcd.print(" ");
             }
//once you press Enter (D) After refilling masks
      if(key == 'D')
        { 
          if(fm_temp > 100)
            { 
              facemask = -1;
            }
          else
             {
               facemask = fm_temp;
             }
        fm_temp = 0;
       } 
     } 
 //*********************************************************   
//if number exceeds 100, reset facemask to -1
    if(facemask== -1)
       {
        lcd.setCursor(0,0);
         lcd.print("Invalid Entry");
            lcd.setCursor(0,1);
                lcd.print("                          ");
        }
//************************************************************
//display of the current amount of masks
         
          lcd.setCursor(0,0);
           lcd.print("Current amount:");
            lcd.setCursor(0,1);
              lcd.print(facemask);  
                lcd.print("             ");
             
//***********************************************************        
//when there is one or more face mask and motion sensor triggered
//***********************************************************       
           
while(facemask>1)
{

//ultrasonic sensor for motion sensing
digitalWrite(trigPin2, LOW);
            delayMicroseconds(2);
              digitalWrite(trigPin2, HIGH);
               delayMicroseconds(10);
                 digitalWrite(trigPin2, LOW);
 

  duration2= pulseIn(echoPin2, HIGH);
  motion= duration2 * 0.034 / 2;
    Serial.print( "Motion: ");
            Serial.print( motion);
               Serial.println ("cm");

//  int newmotion;
//digitalWrite (red,HIGH);

//ultrasonic sensor for mask pick
digitalWrite(trigPin, LOW);
            delayMicroseconds(2);
              digitalWrite(trigPin, HIGH);
               delayMicroseconds(10);
                 digitalWrite(trigPin, LOW);
 

  duration= pulseIn(echoPin, HIGH);
  distance= duration * 0.034 / 2;

          Serial.print( "Distance: ");
            Serial.print( distance);
               Serial.println ("cm");  
 //digitalWrite(red,HIGH);

if (motion<10)
{
  digitalWrite(red,HIGH);
  if (distance<5)
  {
   digitalWrite (green,HIGH);
        facemask--;
        delay (1000);
         lcd.setCursor(0,0);
          lcd.print("current amount :");
            lcd.setCursor(0,1);
              lcd.print(facemask);  
                lcd.print("             ");
           //   newmotion=0;
  }
  }
  
   //case 3: Mask is picked so reduce by one
   
      
              else if (distance >5&& motion>10)
                 {
                   digitalWrite (green,LOW);
                   digitalWrite (red, LOW);
                  
                  }
                  
               } 
//digitalWrite(red,LOW);
               
if (facemask==1)
 {
  lcd.clear();
  lcd.setCursor(0,0);
   lcd.print("Please...             ") ;
    lcd.setCursor(0,1);
     lcd.print("Refill the Masks");
    delay(2000);
  }
                          
         }
